# Fritzing sketch Circuit (saved by Fritzing 0.9.5d)
breadboards: 1

parts:
  M1 = DOIT Esp32 DevKit v1 (30 pins long, 11 pins width) [part_number=ESP32S-PIN30]
  Part1 = Adafruit PAM8302 [part_number="Adafruit #2130"]
  SP1 = SPEAKER [package=pcb_mount_speaker]
  LED1 = smd LED [color="Red (633nm)" package="0805 [SMD]"]
  LED2 = smd LED [color="Green (570nm)" package="0805 [SMD]"]
  LED3 = smd LED [color="Yellow (592nm)" package="0805 [SMD]"]
  R1 = Resistor [tolerance=±5% resistance=330 package="2512 [SMD]"]
  R2 = Resistor [tolerance=±5% resistance=330 package="2512 [SMD]"]
  R3 = Resistor [tolerance=±5% resistance=330 package="2512 [SMD]"]

nets:
  3V3: M1.3V3, Part1.VCC
  GND: M1.GND, Part1.GND, Part1.AIN-, R1.Pin_1, R2.Pin_1, R3.Pin_1
  N1: M1.D32, LED1.anode
  N2: M1.D33, LED3.anode
  N3: M1.D25, Part1.AIN+
  N4: M1.D27, LED2.anode
  N5: M1.D14, Part1.SD
  N6: Part1.VO+, SP1.-
  N7: Part1.VO-, SP1.+

custom parts:
  DOIT Esp32 DevKit v1 (30 pins long, 11 pins width): The DOIT Esp32 DevKit v1 is one of the development board created by DOIT to evaluate the ESP-WROOM-32 module. It is based on the ESP32 microcontroller that boasts Wifi, Bluetooth, Ethernet and Low Power support all in a single chip. (vanepp) made breadboard work, adjusted pin numbering and labels and reduced size of schematic and cleaned up pcb. This chip is 30pins long (2 x15) and 11 pins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
  Adafruit PAM8302: This super small mono amplifier is surprisingly powerful - able to deliver up to 2.5 Watts into 4-8 ohm impedance speakers. Inside the miniature chip is a class D controller, able to run from 2.0V-5.5VDC. Since the amp is a class D, its very efficient (over 90% efficient when driving an 8Ω speaker at over half a Watt) - making it perfect for portable and battery-powered projects. It has built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
